# Fritzing sketch receiver (saved by Fritzing 0.9.3b)
stripboards: 1

parts:
  LM1 = LM741 [part_number=LM741 package="DIP (Dual Inline) [THT]"]
  LM3 = LM741 [part_number=LM741 package="DIP (Dual Inline) [THT]"]
  LM2 = LM741 [part_number=LM741 package="DIP (Dual Inline) [THT]"]
  C4 = Ceramic Capacitor [capacitance=100nF package="200 mil [THT, multilayer]"]
  C6 = Ceramic Capacitor [capacitance=100nF package="200 mil [THT, multilayer]"]
  C7 = Ceramic Capacitor [capacitance=100nF package="200 mil [THT, multilayer]"]
  R1 = Resistor [tolerance=±5% resistance=220 package=THT]
  R2 = Resistor [tolerance=±5% resistance=220 package=THT]
  R3 = Resistor [tolerance=±5% resistance=220 package=THT]
  R4 = Resistor [tolerance=±5% resistance=220 package="0402 [SMD]"]
  C8 = Ceramic Capacitor [capacitance=100nF package="200 mil [THT, multilayer]"]
  C9 = Ceramic Capacitor [capacitance=100nF package="200 mil [THT, multilayer]"]
  MIC1 = Microphone
  R5 = Resistor [tolerance=±5% resistance=220 package="0402 [SMD]"]
  R6 = Resistor [tolerance=±5% resistance=220 package=THT]
  D1 = P1000K [part_number=P1000K]
  R7 = Resistor [tolerance=±5% resistance=220 package="0402 [SMD]"]
  R8 = Resistor [tolerance=±5% resistance=220 package="0402 [SMD]"]

nets:
  N1: LM1.pin2, R3.Pin_1, C8.1
  N2: LM1.pin6, R3.Pin_0, R7.Pin_0
  N3: LM1.pin7, LM3.pin7, LM2.pin7
  N4: LM3.pin2, R1.Pin_1, R6.Pin_1
  N5: LM3.pin6, R6.Pin_0, D1.anode
  N6: LM2.pin2, R2.Pin_1, C9.1
  N7: LM2.pin6, C6.0, C7.1, R2.Pin_0
  N8: C4.0, R4.Pin_1, MIC1.pin1, R5.Pin_1, R8.Pin_1
  N9: C4.1, R5.Pin_0, D1.cathode
  N10: C6.1, C9.0, R7.Pin_1, R8.Pin_0
  N11: C7.0, R1.Pin_0
  N12: R4.Pin_0, C8.0, MIC1.pin2

custom parts:
  LM741: This is a single Op Amp DIP.
